// Logisim project CRC_Module_all.circ as structural Verilog
module ModuloCRCALL (
  input  MD__selects_the_behaviour_of_the_chip,
  input  Line_IN,
  input  Clock,
  input  Reset,
  output Line_OUT,
  output BUSY
);

  wire md_enable_1_p2;

  // MD_Enable md_enable_1: pin names not known; wires that end beside it: Line_IN, md_enable_1_p2
  Shift_Register Delayer__shift_reg (
    .in(md_enable_1_p2), .clk(Clock));  // open: shift, out, load, clr, d0, q0, d1, q1, d2, q2, d3, q3, d4, q4, d5, q5, d6, q6, d7, q7
endmodule

// do_xor
module Do_XOR (
  input  B,
  input  A,
  input  E,
  output C
);

  wire and_1_out;

  and and_1 (and_1_out, A, E);
  xor xor_1 (C, B, and_1_out);
endmodule

module MD_Enable (
  input  MD,
  input  CTRL_OUT,
  input  LINE_IN,
  output REG_IN
);

  wire or_1_out;

  or or_1 (or_1_out, MD, CTRL_OUT);
  and and_1 (REG_IN, or_1_out, LINE_IN);
endmodule
